# Fritzing sketch 02 - Interrupt (saved by Fritzing 0.9.3b)
circuit board: 8.46667cm x 5.64444cm
breadboards: 1

parts:
  Arduino = Arduino Uno (Rev3)
  LED1 = LED - 5mm [color="Red (633nm)" package="5 mm [THT]"]
  R1 = Resistor [tolerance=±5% resistance=1k package=THT]
  S1 = Pushbutton [package="[THT]"]
  R2 = Resistor [tolerance=±5% resistance=1k package=THT]

nets:
  N1: Arduino.D13/SCK, R1.Pin_0
  N2: Arduino.GND, LED1.anode, R2.Pin_1
  N3: Arduino.D2, S1.Pin_1, S1.Pin_2, R2.Pin_0
  N4: Arduino.5V, S1.Pin_3, S1.Pin_4
  N5: LED1.cathode, R1.Pin_1

// code stored in the sketch: 02 - Interrupt.ino
/*   02 - Interupt
 *   
 *   It changes led blink speed when pressing a button.
 *   
 *   It requires a button attached to pin 2 and a led attached to pin 13
 * 
 *   By Chiccodb00 - 26 march 2018
 */

/* PINs DEFINITION */
const byte led = 13;
const byte interruptPin = 2;
/* BLINK SPEED DEFINITION */
const int fastBlinkSpeed = 500;
const int slowBlinkSpeed = 1000;
volatile boolean blinkFast = false;                                          //If true it blinks faster - Change by interrupt
/* TIME AND PIN STATUS TRACKING */
long timeChange = 0;
boolean ledStatus = false;

void setup() {
  /* SET PINs TO INPUT OR OUTPUT */
  pinMode(led, OUTPUT);
  pinMode(interruptPin, INPUT);
  attachInterrupt(digitalPinToInterrupt(interruptPin), changeSpeed, RISING); //Attach interrupt to call the changeSpeed method when value is changing
}

void loop() {
  //This is a way to avoid using the delays
  if(timeChange <= millis()){
    //Invert the led status and turn it on or off based on ledStatus variable
    ledStatus = !ledStatus;
    digitalWrite(led, ledStatus);
    if(blinkFast) timeChange = millis() + fastBlinkSpeed;
    else          timeChange = millis() + slowBlinkSpeed;
  }
}

// Method called by interrupt for change blink speed
void changeSpeed(){
  blinkFast = !blinkFast;
}
